# Fritzing sketch fishing-bot (saved by Fritzing 1.0.4)

parts:
  Load_Cell1 = Load Cell - Red/white/black/green
  Part1 = HX711 Weighing Sensor Module
  Part2 = Arduino Uno (Rev3)
  power1 = DC Motor [voltage_(max)=6V voltage_(min)=3V]  # not connected
  M3 = DC Motor [voltage_(max)=6V voltage_(min)=3V]  # not connected
  X1 = USB Connectors [package=usb-a-s-nosilk-female]
  U1 = mystery part, 3 pins [chip_label=?]

nets:
  N1: Load_Cell1.wire1, Part1.E+
  N2: Load_Cell1.wire2, Part1.A+
  N3: Load_Cell1.wire3, Part1.E-
  N4: Load_Cell1.wire4, Part1.A-
  VCC: Part1.VCC, Part2.5V
  GND: Part1.GND, Part2.GND
  N5: Part1.DO/RX, Part2.D2
  N6: Part1.CK/TX, Part2.D3_PWM
  N7: X1.D-, U1.pin1

notes:
  load cell
  hx711
  dynamixel mx-28r
  U2D2 powerboard
  computer

custom parts:
  Load Cell - Red/white/black/green: A rectangle load cell/weighting pressure Sensor with four wires - Red, white, black, green. Normally corresponding with E+, E-, A+, A- respectively.
  HX711 Weighing Sensor Module: HX711 is a precision 24-bit analog-to-digital converter (ADC) designed for weigh scales and industrial control applications to interface directly with a bridge sensor.
